// Logisim project nit36_lab4.circ as structural Verilog: 1 circuit, main circuit main
module main (
  input  [3:0] A,
  input  [3:0] B,
  input  sub
);

  wire adder_1_cout, SOV, UOV, xor_1_out, xor_3_out;
  wire [3:0] MUX_OUT, not_1_out, O;

  assign not_1_out = ~B;  // NOT_Gate not_1, 4 bits wide
  // Probe on A
  // Probe on B
  // Probe on O
  LED led_1 (.in(UOV));
  Multiplexer #(.width(4)) multiplexer_1 (.in0(B), .in1(not_1_out), .out(MUX_OUT), .sel(sub));  // open: en
  xor xor_1 (xor_1_out, A[3], MUX_OUT[3]);
  // Probe on A
  // Probe on B
  // Probe on O
  LED led_2 (.in(SOV));
  Adder #(.width(4)) adder_1 (.a(A), .b(MUX_OUT), .out(O), .cin(sub), .cout(adder_1_cout));
  xor xor_2 (UOV, adder_1_cout, sub);
  xor xor_3 (xor_3_out, xor_1_out, O[3]);
  not not_2 (SOV, xor_3_out);
endmodule
