// Logisim project nit36_lab5.circ as structural Verilog: 1 circuit, main circuit main
module main (
);

  wire button_1_out, CLK, clock_1_out, subtractor_1_bout;
  wire [15:0] bit_extender_1_out, or_2_out, register_1_q, register_2_q, register_3_q, shifter_1_out,
       shifter_2_out, subtractor_1_out;

  Clock clock_1 (.out(clock_1_out));
  Button button_1 (.out(button_1_out));
  or or_1 (CLK, clock_1_out, button_1_out);
  Register #(.width(16)) register_1 (.D(or_2_out), .Q(register_1_q), .clk(CLK));  // open: en, clr
  Register #(.width(16)) register_2 (.D(shifter_2_out), .Q(register_2_q), .clk(CLK));  // open: en, clr
  Shifter #(.width(16)) shifter_1 (.in(register_1_q), .\dist (4'b0001), .out(shifter_1_out));
  // Probe on register_2_q
  Shifter #(.width(16), .shift("lr")) shifter_2 (.in(register_2_q), .\dist (4'b0001), .out(shifter_2_out));
  Register #(.width(16)) register_3 (.D(subtractor_1_out), .Q(register_3_q), .clk(CLK));  // open: en, clr
  // Probe on shifter_2_out
  assign or_2_out = shifter_1_out | bit_extender_1_out;  // OR_Gate or_2, 16 bits wide
  // Probe on or_2_out
  Subtractor #(.width(16)) subtractor_1 (
    .a(register_3_q), .b(shifter_2_out), .out(subtractor_1_out), .bout(subtractor_1_bout));  // open: bin
  // Probe on subtractor_1_bout
  assign bit_extender_1_out = {{15{1'b0}}, subtractor_1_bout};  // Bit_Extender bit_extender_1

  // Notes on the sheet:
  //   Quotient
  //   Divisor
  //   Dividend/Rem
endmodule
